# Fritzing sketch tarefa 3 (saved by Fritzing 0.9.3b)
breadboards: 1

parts:
  Componente2 = Arduino Uno (Rev3)
  7_Segment2 = 7 Segment Display
  R6 = Resistor [tolerance=±5% resistance=220 package=THT]
  RHT3 = Humidity and Temperature Sensor RHT03 [part_number=DHT22]
  R7 = Resistor [tolerance=±5% resistance=220 package=THT]
  LED3 = RGB LED (com. cathode, rgb) [package="5 mm [THT]"]
  R8 = Resistor [tolerance=±5% resistance=220 package=THT]
  R9 = Rotary Potentiometer (Large) [maximum_resistance=100kΩ package=THT]
  R10 = Resistor [tolerance=±5% resistance=220 package=THT]

nets:
  N1: Componente2.A5/SCL, R9.wiper
  N2: Componente2.D8, RHT3.Data-signal, R8.Pin_0
  N3: Componente2.D9_PWM, LED3.red_anode
  N4: Componente2.D10_PWM/SS, LED3.green_anode
  N5: Componente2.D11_PWM/MOSI, LED3.blue_anode
  N6: Componente2.D12/MISO, 7_Segment2.Segment_D
  N7: Componente2.D1/TX, 7_Segment2.Segment_C
  N8: Componente2.D2, 7_Segment2.Segment_DP
  N9: Componente2.D3_PWM, 7_Segment2.Segment_E
  N10: Componente2.D4, 7_Segment2.Segment_F
  N11: Componente2.D5_PWM, 7_Segment2.Segment_G
  N12: Componente2.D6_PWM, 7_Segment2.Segment_B
  N13: Componente2.D7, 7_Segment2.Segment_A
  5V: Componente2.5V, R6.Pin_1, RHT3.Vcc, R7.Pin_0, R8.Pin_1, R9.leg1
  N14: Componente2.GND, RHT3.GND_2, R9.leg2, R10.Pin_1
  N15: 7_Segment2.common_anode, R6.Pin_0, R7.Pin_1
  N16: LED3.common_cathode, R10.Pin_0
