# Fritzing sketch projeto (saved by Fritzing 0.9.3b)
breadboards: 2

parts:
  Componente2 = Arduino Uno (Rev3)
  RHT3 = Humidity and Temperature Sensor RHT03 [part_number=DHT22]
  LED3 = RGB LED (com. cathode, rgb) [package="5 mm [THT]"]
  R8 = Resistor [tolerance=±5% resistance=220 package=THT]
  R9 = Rotary Potentiometer (Large) [maximum_resistance=100kΩ package=THT]
  R10 = Resistor [tolerance=±5% resistance=220 package=THT]
  J1 = Basic Servo
  Componente3 = Arduino Uno (Rev3)
  U1 = RF-LINK_TX [package=rf-link_tx]  # not connected
  U2 = RF-LINK_RX [package=rf-link_rx]
  U3 = 7-SEGMENT-DISPLAY [package=7-segment-display]
  R11 = Resistor [tolerance=±5% resistance=220 package=THT]
  R12 = Resistor [tolerance=±5% resistance=220 package=THT]

nets:
  N1: Componente2.A5/SCL, R9.wiper
  N2: Componente2.D8, U3.G2
  N3: Componente2.D9_PWM, U3.A
  N4: Componente2.D10_PWM/SS, U3.DP
  N5: Componente2.D11_PWM/MOSI, U3.B
  N6: Componente2.D12/MISO, U3.G1
  N7: Componente2.D13/SCK, U3.D
  N8: Componente2.D1/TX, U2.DATA
  N9: Componente2.D2, U3.G
  N10: Componente2.D3_PWM, J1.pulse
  N11: Componente2.D4, U3.E
  N12: Componente2.D5_PWM, LED3.red_anode
  N13: Componente2.D6_PWM, LED3.green_anode
  N14: Componente2.D7, LED3.blue_anode
  5V: Componente2.5V, R9.leg1, U2.+5V, R11.Pin_1, R12.Pin_0
  GND: Componente2.GND, R9.leg2, R10.Pin_1, U2.GND
  VCC: RHT3.Vcc, RHT3.Data-signal, R8.Pin_0, R8.Pin_1, Componente3.D8, Componente3.5V
  N15: RHT3.GND_2, Componente3.GND
  N16: LED3.common_cathode, R10.Pin_0
  N17: U3.C, R12.Pin_1
  N18: U3.F, R11.Pin_0
